# Fritzing sketch lpc1114_bell (saved by Fritzing 0.9.2b)
breadboards: 3

parts:
  IC1 = lpc1114
  JP1 = usb_mpl2303sa
  S6 = Pushbutton [package="[THT]"]
  S7 = Toggle Switch [package=THT]
  LED1 = LED - 5mm [color="Blue (525nm)" package="5 mm [THT]"]
  R1 = Resistor [tolerance=±5% resistance=1k package=THT]
  J1 = Piezo Speaker

nets:
  N1: IC1.connector3, R1.Pin_0
  N2: IC1.connector14, JP1.connector2
  N3: IC1.connector15, JP1.connector4
  N4: IC1.connector21, JP1.connector1, LED1.cathode
  N5: IC1.connector22, S6.Pin_3, S6.Pin_4
  N6: IC1.connector23, S7.L2
  N7: IC1.connector27, LED1.anode
  N8: S6.Pin_1, S6.Pin_2, S7.COM
  N9: R1.Pin_1, J1.pin2
